// Logisim project synch.circ as structural Verilog: 1 circuit, main circuit main
module main (
  input  r1_prime,
  input  r1,
  input  r2,
  input  r2_prime,
  input  x,
  input  a,
  input  b,
  output Example_Fits,
  output out_9
);

  wire and_1_out, and_2_out, and_3_out, and_4_out, and_5_out, nor_1_out, nor_2_out, nor_3_out, not_1_out,
       or_2_out, or_3_out, or_4_out, xor_1_out;

  xor xor_1 (xor_1_out, r1, x);
  not not_1 (not_1_out, x);
  nor nor_1 (nor_1_out, a, b);
  and and_1 (and_1_out, b, a);
  and and_2 (and_2_out, r2, not_1_out);
  and and_3 (and_3_out, r1, x);
  or or_1 (out_9, nor_1_out, and_1_out);
  nor nor_2 (nor_2_out, xor_1_out, r1_prime);
  and and_4 (and_4_out, r1_prime, xor_1_out);
  or or_2 (or_2_out, and_2_out, and_3_out);
  or or_3 (or_3_out, nor_2_out, and_4_out);
  nor nor_3 (nor_3_out, or_2_out, r2_prime);
  and and_5 (and_5_out, r2_prime, or_2_out);
  or or_4 (or_4_out, nor_3_out, and_5_out);
  and and_6 (Example_Fits, or_3_out, or_4_out);

  // Notes on the sheet:
  //   a <-> b
endmodule
